# Fritzing sketch tft_st7789_sketch (saved by Fritzing 1.0.3b)
breadboards: 1

parts:
  esp1 = ESP32 DevKitc V4
  LCD1 = TFT 1.8 inch 160x128 w SD

nets:
  N1: esp1.IO5, LCD1.Pin_11
  N2: esp1.IO18, LCD1.Pin_7
  N3: esp1.IO22, LCD1.Pin_10
  N4: esp1.IO23, LCD1.Pin_6
  N5: esp1.GND, LCD1.Pin_2, LCD1.Pin_3
  N6: esp1.3V3, LCD1.Pin_1, LCD1.Pin_4
  N7: esp1.CLK, LCD1.Pin_5

custom parts:
  ESP32 DevKitc V4: ESP32-DevKitC board with ESP32-WROOM-32 module. ESP32-DevKitC V4 is a small-sized ESP32-based development board produced by Espressif. Most of the pins on the ESP module are broken out to the pin headers on the board. The pins D0, D1, D2, D3, CMD and CLK are used internally for communication between ESP32 and SPI flash memory. They are grouped on both sides near the USB connector. Avoid using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
  TFT 1.8 inch 160x128 w SD: This is a generic 1.8 tft spi lcd display available on ebay and others. The 1.8" display has 128x160 color pixels and in this version pin names in breadboard (unlike the real board).
